// Logisim project 8 Mux.circ as structural Verilog: 1 circuit, main circuit main
module main (
);

  wire and_1_out, and_2_out, and_3_out, and_4_out, and_5_out, and_6_out, and_7_out, and_8_out, and_9_out,
       and_10_out, and_11_out, and_12_out, and_13_out, and_14_out, and_15_out, and_16_out, not_1_out,
       not_2_out, not_3_out, not_4_out, not_5_out, not_6_out, not_7_out, not_8_out, or_1_out, or_2_out,
       or_3_out, or_4_out, or_5_out, or_6_out, or_7_out, or_8_out, undriven, undriven_2, undriven_3,
       undriven_4, undriven_5, undriven_6, undriven_7, undriven_8, undriven_9, undriven_10, undriven_11,
       undriven_12, undriven_13, undriven_14, undriven_15, undriven_16, undriven_17, undriven_18,
       undriven_19, undriven_20, undriven_21, undriven_22, undriven_23, undriven_24;

  not not_1 (not_1_out, undriven_2);
  not not_2 (not_2_out, undriven_5);
  not not_3 (not_3_out, undriven_8);
  not not_4 (not_4_out, undriven_11);
  not not_5 (not_5_out, undriven_14);
  not not_6 (not_6_out, undriven_17);
  not not_7 (not_7_out, undriven_20);
  not not_8 (not_8_out, undriven_23);
  and and_1 (and_1_out, undriven, not_1_out);
  and and_2 (and_2_out, undriven_2, undriven_3);
  and and_3 (and_3_out, undriven_4, not_2_out);
  and and_4 (and_4_out, undriven_5, undriven_6);
  and and_5 (and_5_out, undriven_7, not_3_out);
  and and_6 (and_6_out, undriven_8, undriven_9);
  and and_7 (and_7_out, undriven_10, not_4_out);
  and and_8 (and_8_out, undriven_11, undriven_12);
  and and_9 (and_9_out, undriven_13, not_5_out);
  and and_10 (and_10_out, undriven_14, undriven_15);
  and and_11 (and_11_out, undriven_16, not_6_out);
  and and_12 (and_12_out, undriven_17, undriven_18);
  and and_13 (and_13_out, undriven_19, not_7_out);
  and and_14 (and_14_out, undriven_20, undriven_21);
  and and_15 (and_15_out, undriven_22, not_8_out);
  and and_16 (and_16_out, undriven_23, undriven_24);
  or or_1 (or_1_out, and_1_out, and_2_out);
  or or_2 (or_2_out, and_3_out, and_4_out);
  or or_3 (or_3_out, and_5_out, and_6_out);
  or or_4 (or_4_out, and_7_out, and_8_out);
  or or_5 (or_5_out, and_9_out, and_10_out);
  or or_6 (or_6_out, and_11_out, and_12_out);
  or or_7 (or_7_out, and_13_out, and_14_out);
  or or_8 (or_8_out, and_15_out, and_16_out);
endmodule
