// Logisim project 8 bit register.circ as structural Verilog: 1 circuit, main circuit main
module main (
  input  in_1,
  input  in_2,
  input  in_3,
  input  in_4,
  input  in_5,
  input  in_6,
  input  in_7,
  input  in_8,
  output out_9,
  output out_10,
  output out_11,
  output out_12,
  output out_13,
  output out_14,
  output out_15,
  output out_16,
  output out_17,
  output out_18,
  output out_19,
  output out_20,
  output out_21,
  output out_22,
  output out_23,
  output out_24
);

  wire E_out, nand_1_out, nand_2_out, nand_3_out, nand_4_out, nand_5_out, nand_6_out, nand_7_out, nand_8_out,
       nand_9_out, nand_10_out, nand_11_out, nand_12_out, nand_13_out, nand_14_out, nand_15_out, nand_16_out,
       nand_17_out, nand_18_out, nand_19_out, nand_20_out, nand_21_out, nand_22_out, nand_23_out,
       nand_24_out, nand_25_out, nand_26_out, nand_27_out, nand_28_out, nand_29_out, nand_30_out,
       nand_31_out, nand_32_out, nand_33_out, nand_34_out, nand_35_out, nand_36_out, nand_37_out,
       nand_38_out, nand_39_out, nand_40_out, nand_41_out, nand_42_out, nand_43_out, nand_44_out,
       nand_45_out, nand_46_out, nand_47_out, nand_48_out, not_1_out, not_2_out, not_3_out, not_4_out,
       not_5_out, not_6_out, not_7_out, not_8_out, not_9_out, not_10_out, not_11_out, not_12_out, not_13_out,
       not_14_out, not_15_out, not_16_out, not_17_out, not_18_out, not_19_out, not_20_out, not_21_out,
       not_22_out, not_23_out, not_24_out, not_25_out, not_26_out, not_27_out, not_28_out, not_29_out,
       not_30_out, not_31_out, not_32_out;

  Clock E (.out(E_out));
  not not_1 (not_1_out, in_1);
  not not_2 (not_2_out, E_out);
  not not_3 (not_3_out, in_2);
  not not_4 (not_4_out, E_out);
  not not_5 (not_5_out, in_3);
  not not_6 (not_6_out, E_out);
  not not_7 (not_7_out, in_4);
  not not_8 (not_8_out, E_out);
  not not_9 (not_9_out, in_5);
  not not_10 (not_10_out, E_out);
  not not_11 (not_11_out, in_6);
  not not_12 (not_12_out, E_out);
  not not_13 (not_13_out, in_7);
  not not_14 (not_14_out, E_out);
  not not_15 (not_15_out, in_8);
  not not_16 (not_16_out, E_out);
  nand nand_1 (nand_1_out, in_1, not_2_out);
  nand nand_2 (nand_2_out, not_2_out, not_1_out);
  nand nand_3 (nand_3_out, in_2, not_4_out);
  nand nand_4 (nand_4_out, not_4_out, not_3_out);
  nand nand_5 (nand_5_out, in_3, not_6_out);
  nand nand_6 (nand_6_out, not_6_out, not_5_out);
  nand nand_7 (nand_7_out, in_4, not_8_out);
  nand nand_8 (nand_8_out, not_8_out, not_7_out);
  nand nand_9 (nand_9_out, in_5, not_10_out);
  nand nand_10 (nand_10_out, not_10_out, not_9_out);
  nand nand_11 (nand_11_out, in_6, not_12_out);
  nand nand_12 (nand_12_out, not_12_out, not_11_out);
  nand nand_13 (nand_13_out, in_7, not_14_out);
  nand nand_14 (nand_14_out, not_14_out, not_13_out);
  nand nand_15 (nand_15_out, in_8, not_16_out);
  nand nand_16 (nand_16_out, not_16_out, not_15_out);
  nand nand_17 (nand_17_out, nand_1_out, nand_18_out);
  nand nand_18 (nand_18_out, nand_17_out, nand_2_out);
  nand nand_19 (nand_19_out, nand_3_out, nand_20_out);
  nand nand_20 (nand_20_out, nand_19_out, nand_4_out);
  nand nand_21 (nand_21_out, nand_5_out, nand_22_out);
  nand nand_22 (nand_22_out, nand_21_out, nand_6_out);
  nand nand_23 (nand_23_out, nand_7_out, nand_24_out);
  nand nand_24 (nand_24_out, nand_23_out, nand_8_out);
  nand nand_25 (nand_25_out, nand_9_out, nand_26_out);
  nand nand_26 (nand_26_out, nand_25_out, nand_10_out);
  nand nand_27 (nand_27_out, nand_11_out, nand_28_out);
  nand nand_28 (nand_28_out, nand_27_out, nand_12_out);
  nand nand_29 (nand_29_out, nand_13_out, nand_30_out);
  nand nand_30 (nand_30_out, nand_29_out, nand_14_out);
  nand nand_31 (nand_31_out, nand_15_out, nand_32_out);
  nand nand_32 (nand_32_out, nand_31_out, nand_16_out);
  not not_17 (not_17_out, not_2_out);
  not not_18 (not_18_out, not_4_out);
  not not_19 (not_19_out, not_6_out);
  not not_20 (not_20_out, not_8_out);
  not not_21 (not_21_out, not_10_out);
  not not_22 (not_22_out, not_12_out);
  not not_23 (not_23_out, not_14_out);
  not not_24 (not_24_out, not_16_out);
  not not_25 (not_25_out, nand_17_out);
  not not_26 (not_26_out, nand_19_out);
  not not_27 (not_27_out, nand_21_out);
  not not_28 (not_28_out, nand_23_out);
  not not_29 (not_29_out, nand_25_out);
  not not_30 (not_30_out, nand_27_out);
  not not_31 (not_31_out, nand_29_out);
  not not_32 (not_32_out, nand_31_out);
  nand nand_33 (nand_33_out, nand_17_out, not_17_out);
  nand nand_34 (nand_34_out, not_17_out, not_25_out);
  nand nand_35 (nand_35_out, nand_19_out, not_18_out);
  nand nand_36 (nand_36_out, not_18_out, not_26_out);
  nand nand_37 (nand_37_out, nand_21_out, not_19_out);
  nand nand_38 (nand_38_out, not_19_out, not_27_out);
  nand nand_39 (nand_39_out, nand_23_out, not_20_out);
  nand nand_40 (nand_40_out, not_20_out, not_28_out);
  nand nand_41 (nand_41_out, nand_25_out, not_21_out);
  nand nand_42 (nand_42_out, not_21_out, not_29_out);
  nand nand_43 (nand_43_out, nand_27_out, not_22_out);
  nand nand_44 (nand_44_out, not_22_out, not_30_out);
  nand nand_45 (nand_45_out, nand_29_out, not_23_out);
  nand nand_46 (nand_46_out, not_23_out, not_31_out);
  nand nand_47 (nand_47_out, nand_31_out, not_24_out);
  nand nand_48 (nand_48_out, not_24_out, not_32_out);
  nand nand_49 (out_9, nand_33_out, out_10);
  nand nand_50 (out_10, out_9, nand_34_out);
  nand nand_51 (out_11, nand_35_out, out_12);
  nand nand_52 (out_12, out_11, nand_36_out);
  nand nand_53 (out_13, nand_37_out, out_14);
  nand nand_54 (out_14, out_13, nand_38_out);
  nand nand_55 (out_15, nand_39_out, out_16);
  nand nand_56 (out_16, out_15, nand_40_out);
  nand nand_57 (out_17, nand_41_out, out_18);
  nand nand_58 (out_18, out_17, nand_42_out);
  nand nand_59 (out_19, nand_43_out, out_20);
  nand nand_60 (out_20, out_19, nand_44_out);
  nand nand_61 (out_21, nand_45_out, out_22);
  nand nand_62 (out_22, out_21, nand_46_out);
  nand nand_63 (out_23, nand_47_out, out_24);
  nand nand_64 (out_24, out_23, nand_48_out);
endmodule
