// Logisim project Complete Ram module.circ as structural Verilog: 1 circuit, main circuit main
module main (
  input  in_1,
  input  in_2,
  input  in_3,
  input  G,
  input  in_5,
  input  in_6,
  input  in_7,
  input  S,
  input  in_9,
  input  in_10,
  output out_11,
  output out_12,
  output out_13,
  output out_14,
  output out_15,
  output out_16,
  output out_17,
  output out_18
);

  wire and_1_out, and_2_out, and_3_out, and_4_out, and_5_out, and_6_out, and_7_out, and_8_out, and_9_out,
       and_10_out, and_11_out, and_12_out, and_13_out, and_14_out, and_15_out, and_16_out, and_17_out,
       and_18_out, nand_1_out, nand_2_out, nand_3_out, nand_4_out, nand_5_out, nand_6_out, nand_7_out,
       nand_8_out, nand_9_out, nand_10_out, nand_11_out, nand_12_out, nand_13_out, nand_14_out, nand_15_out,
       nand_16_out, nand_17_out, nand_18_out, nand_19_out, nand_20_out, nand_21_out, nand_22_out,
       nand_23_out, nand_24_out, nand_25_out, nand_26_out, nand_27_out, nand_28_out, nand_29_out,
       nand_30_out, nand_31_out, nand_32_out, nand_33_out, nand_34_out, nand_35_out, nand_36_out,
       nand_37_out, nand_38_out, nand_39_out, nand_40_out, nand_41_out, nand_42_out, nand_43_out,
       nand_44_out, nand_45_out, nand_46_out, nand_47_out, nand_48_out, nand_49_out, nand_50_out,
       nand_51_out, nand_52_out, nand_53_out, nand_54_out, nand_55_out, nand_56_out, nand_57_out,
       nand_58_out, nand_59_out, nand_60_out, nand_61_out, nand_62_out, nand_63_out, nand_64_out,
       nand_65_out, nand_66_out, nand_67_out, nand_68_out, nand_69_out, nand_70_out, nand_71_out,
       nand_72_out, nand_73_out, nand_74_out, nand_75_out, nand_76_out, nand_77_out, nand_78_out,
       nand_79_out, nand_80_out, nand_81_out, nand_82_out, nand_83_out, nand_84_out, nand_85_out,
       nand_86_out, nand_87_out, nand_88_out, nand_89_out, nand_90_out, nand_91_out, nand_92_out,
       nand_93_out, nand_94_out, nand_95_out, nand_96_out, nand_97_out, nand_98_out, nand_99_out,
       nand_100_out, nand_101_out, nand_102_out, nand_103_out, nand_104_out, nand_105_out, nand_106_out,
       nand_107_out, nand_108_out, nand_109_out, nand_110_out, nand_111_out, nand_112_out, nand_113_out,
       nand_114_out, nand_115_out, nand_116_out, nand_117_out, nand_118_out, nand_119_out, nand_120_out,
       nand_121_out, nand_122_out, nand_123_out, nand_124_out, nand_125_out, nand_126_out, nand_127_out,
       nand_128_out, not_1_out, not_2_out, not_3_out, not_4_out, not_5_out, not_6_out, not_7_out, not_8_out,
       not_9_out, not_10_out, not_11_out, not_12_out, not_13_out, not_14_out, not_15_out, not_16_out,
       not_17_out, not_18_out, not_19_out, not_20_out, not_21_out, not_22_out, not_23_out, not_24_out,
       not_25_out, not_26_out, not_27_out, not_28_out, not_29_out, not_30_out, not_31_out, not_32_out,
       not_33_out, not_34_out, not_35_out, not_36_out, not_37_out, not_38_out, not_39_out, not_40_out,
       not_41_out, not_42_out, not_43_out, not_44_out, not_45_out, not_46_out, not_47_out, not_48_out,
       not_49_out, not_50_out, not_51_out, not_52_out, not_53_out, not_54_out, not_55_out, not_56_out,
       not_57_out, not_58_out, not_59_out, not_60_out, not_61_out, not_62_out, not_63_out, not_64_out,
       not_65_out, not_66_out, not_67_out, not_68_out, not_69_out, not_70_out, not_71_out, not_72_out,
       not_73_out;

  not not_1 (not_1_out, S);
  and and_1 (and_1_out, G, not_1_out);
  and and_2 (and_2_out, G, S);
  not not_2 (not_2_out, in_1);
  not not_3 (not_3_out, and_1_out);
  not not_4 (not_4_out, in_2);
  not not_5 (not_5_out, and_1_out);
  not not_6 (not_6_out, in_3);
  not not_7 (not_7_out, and_1_out);
  not not_8 (not_8_out, in_5);
  not not_9 (not_9_out, and_1_out);
  not not_10 (not_10_out, in_6);
  not not_11 (not_11_out, and_1_out);
  not not_12 (not_12_out, in_7);
  not not_13 (not_13_out, and_1_out);
  not not_14 (not_14_out, in_9);
  not not_15 (not_15_out, and_1_out);
  not not_16 (not_16_out, in_10);
  not not_17 (not_17_out, and_1_out);
  not not_18 (not_18_out, in_1);
  not not_19 (not_19_out, and_2_out);
  not not_20 (not_20_out, in_2);
  not not_21 (not_21_out, and_2_out);
  not not_22 (not_22_out, in_3);
  not not_23 (not_23_out, and_2_out);
  not not_24 (not_24_out, in_5);
  not not_25 (not_25_out, and_2_out);
  not not_26 (not_26_out, in_6);
  not not_27 (not_27_out, and_2_out);
  not not_28 (not_28_out, in_7);
  not not_29 (not_29_out, and_2_out);
  not not_30 (not_30_out, in_9);
  not not_31 (not_31_out, and_2_out);
  not not_32 (not_32_out, in_10);
  not not_33 (not_33_out, and_2_out);
  nand nand_1 (nand_1_out, in_1, not_3_out);
  nand nand_2 (nand_2_out, not_3_out, not_2_out);
  nand nand_3 (nand_3_out, in_2, not_5_out);
  nand nand_4 (nand_4_out, not_5_out, not_4_out);
  nand nand_5 (nand_5_out, in_3, not_7_out);
  nand nand_6 (nand_6_out, not_7_out, not_6_out);
  nand nand_7 (nand_7_out, in_5, not_9_out);
  nand nand_8 (nand_8_out, not_9_out, not_8_out);
  nand nand_9 (nand_9_out, in_6, not_11_out);
  nand nand_10 (nand_10_out, not_11_out, not_10_out);
  nand nand_11 (nand_11_out, in_7, not_13_out);
  nand nand_12 (nand_12_out, not_13_out, not_12_out);
  nand nand_13 (nand_13_out, in_9, not_15_out);
  nand nand_14 (nand_14_out, not_15_out, not_14_out);
  nand nand_15 (nand_15_out, in_10, not_17_out);
  nand nand_16 (nand_16_out, not_17_out, not_16_out);
  nand nand_17 (nand_17_out, in_1, not_19_out);
  nand nand_18 (nand_18_out, not_19_out, not_18_out);
  nand nand_19 (nand_19_out, in_2, not_21_out);
  nand nand_20 (nand_20_out, not_21_out, not_20_out);
  nand nand_21 (nand_21_out, in_3, not_23_out);
  nand nand_22 (nand_22_out, not_23_out, not_22_out);
  nand nand_23 (nand_23_out, in_5, not_25_out);
  nand nand_24 (nand_24_out, not_25_out, not_24_out);
  nand nand_25 (nand_25_out, in_6, not_27_out);
  nand nand_26 (nand_26_out, not_27_out, not_26_out);
  nand nand_27 (nand_27_out, in_7, not_29_out);
  nand nand_28 (nand_28_out, not_29_out, not_28_out);
  nand nand_29 (nand_29_out, in_9, not_31_out);
  nand nand_30 (nand_30_out, not_31_out, not_30_out);
  nand nand_31 (nand_31_out, in_10, not_33_out);
  nand nand_32 (nand_32_out, not_33_out, not_32_out);
  nand nand_33 (nand_33_out, nand_1_out, nand_34_out);
  nand nand_34 (nand_34_out, nand_33_out, nand_2_out);
  nand nand_35 (nand_35_out, nand_3_out, nand_36_out);
  nand nand_36 (nand_36_out, nand_35_out, nand_4_out);
  nand nand_37 (nand_37_out, nand_5_out, nand_38_out);
  nand nand_38 (nand_38_out, nand_37_out, nand_6_out);
  nand nand_39 (nand_39_out, nand_7_out, nand_40_out);
  nand nand_40 (nand_40_out, nand_39_out, nand_8_out);
  nand nand_41 (nand_41_out, nand_9_out, nand_42_out);
  nand nand_42 (nand_42_out, nand_41_out, nand_10_out);
  nand nand_43 (nand_43_out, nand_11_out, nand_44_out);
  nand nand_44 (nand_44_out, nand_43_out, nand_12_out);
  nand nand_45 (nand_45_out, nand_13_out, nand_46_out);
  nand nand_46 (nand_46_out, nand_45_out, nand_14_out);
  nand nand_47 (nand_47_out, nand_15_out, nand_48_out);
  nand nand_48 (nand_48_out, nand_47_out, nand_16_out);
  nand nand_49 (nand_49_out, nand_17_out, nand_50_out);
  nand nand_50 (nand_50_out, nand_49_out, nand_18_out);
  nand nand_51 (nand_51_out, nand_19_out, nand_52_out);
  nand nand_52 (nand_52_out, nand_51_out, nand_20_out);
  nand nand_53 (nand_53_out, nand_21_out, nand_54_out);
  nand nand_54 (nand_54_out, nand_53_out, nand_22_out);
  nand nand_55 (nand_55_out, nand_23_out, nand_56_out);
  nand nand_56 (nand_56_out, nand_55_out, nand_24_out);
  nand nand_57 (nand_57_out, nand_25_out, nand_58_out);
  nand nand_58 (nand_58_out, nand_57_out, nand_26_out);
  nand nand_59 (nand_59_out, nand_27_out, nand_60_out);
  nand nand_60 (nand_60_out, nand_59_out, nand_28_out);
  nand nand_61 (nand_61_out, nand_29_out, nand_62_out);
  nand nand_62 (nand_62_out, nand_61_out, nand_30_out);
  nand nand_63 (nand_63_out, nand_31_out, nand_64_out);
  nand nand_64 (nand_64_out, nand_63_out, nand_32_out);
  not not_34 (not_34_out, not_3_out);
  not not_35 (not_35_out, not_5_out);
  not not_36 (not_36_out, not_7_out);
  not not_37 (not_37_out, not_9_out);
  not not_38 (not_38_out, not_11_out);
  not not_39 (not_39_out, not_13_out);
  not not_40 (not_40_out, not_15_out);
  not not_41 (not_41_out, not_17_out);
  not not_42 (not_42_out, not_19_out);
  not not_43 (not_43_out, not_21_out);
  not not_44 (not_44_out, not_23_out);
  not not_45 (not_45_out, not_25_out);
  not not_46 (not_46_out, not_27_out);
  not not_47 (not_47_out, not_29_out);
  not not_48 (not_48_out, not_31_out);
  not not_49 (not_49_out, not_33_out);
  not not_50 (not_50_out, nand_33_out);
  not not_51 (not_51_out, nand_35_out);
  not not_52 (not_52_out, nand_37_out);
  not not_53 (not_53_out, nand_39_out);
  not not_54 (not_54_out, nand_41_out);
  not not_55 (not_55_out, nand_43_out);
  not not_56 (not_56_out, nand_45_out);
  not not_57 (not_57_out, nand_47_out);
  not not_58 (not_58_out, nand_49_out);
  not not_59 (not_59_out, nand_51_out);
  not not_60 (not_60_out, nand_53_out);
  not not_61 (not_61_out, nand_55_out);
  not not_62 (not_62_out, nand_57_out);
  not not_63 (not_63_out, nand_59_out);
  not not_64 (not_64_out, nand_61_out);
  not not_65 (not_65_out, nand_63_out);
  nand nand_65 (nand_65_out, nand_33_out, not_34_out);
  nand nand_66 (nand_66_out, not_34_out, not_50_out);
  nand nand_67 (nand_67_out, nand_35_out, not_35_out);
  nand nand_68 (nand_68_out, not_35_out, not_51_out);
  nand nand_69 (nand_69_out, nand_37_out, not_36_out);
  nand nand_70 (nand_70_out, not_36_out, not_52_out);
  nand nand_71 (nand_71_out, nand_39_out, not_37_out);
  nand nand_72 (nand_72_out, not_37_out, not_53_out);
  nand nand_73 (nand_73_out, nand_41_out, not_38_out);
  nand nand_74 (nand_74_out, not_38_out, not_54_out);
  nand nand_75 (nand_75_out, nand_43_out, not_39_out);
  nand nand_76 (nand_76_out, not_39_out, not_55_out);
  nand nand_77 (nand_77_out, nand_45_out, not_40_out);
  nand nand_78 (nand_78_out, not_40_out, not_56_out);
  nand nand_79 (nand_79_out, nand_47_out, not_41_out);
  nand nand_80 (nand_80_out, not_41_out, not_57_out);
  nand nand_81 (nand_81_out, nand_49_out, not_42_out);
  nand nand_82 (nand_82_out, not_42_out, not_58_out);
  nand nand_83 (nand_83_out, nand_51_out, not_43_out);
  nand nand_84 (nand_84_out, not_43_out, not_59_out);
  nand nand_85 (nand_85_out, nand_53_out, not_44_out);
  nand nand_86 (nand_86_out, not_44_out, not_60_out);
  nand nand_87 (nand_87_out, nand_55_out, not_45_out);
  nand nand_88 (nand_88_out, not_45_out, not_61_out);
  nand nand_89 (nand_89_out, nand_57_out, not_46_out);
  nand nand_90 (nand_90_out, not_46_out, not_62_out);
  nand nand_91 (nand_91_out, nand_59_out, not_47_out);
  nand nand_92 (nand_92_out, not_47_out, not_63_out);
  nand nand_93 (nand_93_out, nand_61_out, not_48_out);
  nand nand_94 (nand_94_out, not_48_out, not_64_out);
  nand nand_95 (nand_95_out, nand_63_out, not_49_out);
  nand nand_96 (nand_96_out, not_49_out, not_65_out);
  nand nand_97 (nand_97_out, nand_65_out, nand_98_out);
  nand nand_98 (nand_98_out, nand_97_out, nand_66_out);
  nand nand_99 (nand_99_out, nand_67_out, nand_100_out);
  nand nand_100 (nand_100_out, nand_99_out, nand_68_out);
  nand nand_101 (nand_101_out, nand_69_out, nand_102_out);
  nand nand_102 (nand_102_out, nand_101_out, nand_70_out);
  nand nand_103 (nand_103_out, nand_71_out, nand_104_out);
  nand nand_104 (nand_104_out, nand_103_out, nand_72_out);
  nand nand_105 (nand_105_out, nand_73_out, nand_106_out);
  nand nand_106 (nand_106_out, nand_105_out, nand_74_out);
  nand nand_107 (nand_107_out, nand_75_out, nand_108_out);
  nand nand_108 (nand_108_out, nand_107_out, nand_76_out);
  nand nand_109 (nand_109_out, nand_77_out, nand_110_out);
  nand nand_110 (nand_110_out, nand_109_out, nand_78_out);
  nand nand_111 (nand_111_out, nand_79_out, nand_112_out);
  nand nand_112 (nand_112_out, nand_111_out, nand_80_out);
  nand nand_113 (nand_113_out, nand_81_out, nand_114_out);
  nand nand_114 (nand_114_out, nand_113_out, nand_82_out);
  nand nand_115 (nand_115_out, nand_83_out, nand_116_out);
  nand nand_116 (nand_116_out, nand_115_out, nand_84_out);
  nand nand_117 (nand_117_out, nand_85_out, nand_118_out);
  nand nand_118 (nand_118_out, nand_117_out, nand_86_out);
  nand nand_119 (nand_119_out, nand_87_out, nand_120_out);
  nand nand_120 (nand_120_out, nand_119_out, nand_88_out);
  nand nand_121 (nand_121_out, nand_89_out, nand_122_out);
  nand nand_122 (nand_122_out, nand_121_out, nand_90_out);
  nand nand_123 (nand_123_out, nand_91_out, nand_124_out);
  nand nand_124 (nand_124_out, nand_123_out, nand_92_out);
  nand nand_125 (nand_125_out, nand_93_out, nand_126_out);
  nand nand_126 (nand_126_out, nand_125_out, nand_94_out);
  nand nand_127 (nand_127_out, nand_95_out, nand_128_out);
  nand nand_128 (nand_128_out, nand_127_out, nand_96_out);
  not not_66 (not_66_out, and_2_out);
  not not_67 (not_67_out, and_2_out);
  not not_68 (not_68_out, and_2_out);
  not not_69 (not_69_out, and_2_out);
  not not_70 (not_70_out, and_2_out);
  not not_71 (not_71_out, and_2_out);
  not not_72 (not_72_out, and_2_out);
  not not_73 (not_73_out, and_2_out);
  and and_3 (and_3_out, nand_97_out, not_66_out);
  and and_4 (and_4_out, and_2_out, nand_113_out);
  and and_5 (and_5_out, nand_99_out, not_67_out);
  and and_6 (and_6_out, and_2_out, nand_115_out);
  and and_7 (and_7_out, nand_101_out, not_68_out);
  and and_8 (and_8_out, and_2_out, nand_117_out);
  and and_9 (and_9_out, nand_103_out, not_69_out);
  and and_10 (and_10_out, and_2_out, nand_119_out);
  and and_11 (and_11_out, nand_105_out, not_70_out);
  and and_12 (and_12_out, and_2_out, nand_121_out);
  and and_13 (and_13_out, nand_107_out, not_71_out);
  and and_14 (and_14_out, and_2_out, nand_123_out);
  and and_15 (and_15_out, nand_109_out, not_72_out);
  and and_16 (and_16_out, and_2_out, nand_125_out);
  and and_17 (and_17_out, nand_111_out, not_73_out);
  and and_18 (and_18_out, and_2_out, nand_127_out);
  or or_1 (out_11, and_3_out, and_4_out);
  or or_2 (out_12, and_5_out, and_6_out);
  or or_3 (out_13, and_7_out, and_8_out);
  or or_4 (out_14, and_9_out, and_10_out);
  or or_5 (out_15, and_11_out, and_12_out);
  or or_6 (out_16, and_13_out, and_14_out);
  or or_7 (out_17, and_15_out, and_16_out);
  or or_8 (out_18, and_17_out, and_18_out);
endmodule
