// Logisim project Datacell.circ as structural Verilog: 1 circuit, main circuit main
module main (
  input  in_1,
  input  in_2,
  output out_3,
  output out_4,
  output out_5,
  output out_6
);

  wire E_2_out, E_out, nand_1_out, nand_2_out, nand_3_out, nand_4_out, nand_7_out, nand_8_out, nand_9_out,
       nand_10_out, not_1_out, not_2_out, not_3_out, not_4_out, not_5_out;

  Clock E (.out(E_out));
  Clock E_2 (.out(E_2_out));
  not not_1 (not_1_out, in_2);
  not not_2 (not_2_out, E_out);
  not not_3 (not_3_out, in_1);
  nand nand_1 (nand_1_out, in_1, E_2_out);
  nand nand_2 (nand_2_out, not_3_out, E_2_out);
  nand nand_3 (nand_3_out, in_2, not_2_out);
  nand nand_4 (nand_4_out, not_2_out, not_1_out);
  nand nand_5 (out_3, nand_1_out, out_4);
  nand nand_6 (out_4, out_3, nand_2_out);
  nand nand_7 (nand_7_out, nand_3_out, nand_8_out);
  nand nand_8 (nand_8_out, nand_7_out, nand_4_out);
  not not_4 (not_4_out, not_2_out);
  not not_5 (not_5_out, nand_7_out);
  nand nand_9 (nand_9_out, nand_7_out, not_4_out);
  nand nand_10 (nand_10_out, not_4_out, not_5_out);
  nand nand_11 (out_5, nand_9_out, out_6);
  nand nand_12 (out_6, out_5, nand_10_out);

  // Notes on the sheet:
  //   D-Type Flip Flop
  //   Rising Edge-Triggered D-Type Flip Flop
endmodule
